// Logisim project 5BitAdder-Substractor(Con Display).circ as structural Verilog: 1 circuit, main circuit main
module main (
  input  in_1,
  input  in_2,
  input  in_3,
  input  in_4,
  input  in_5,
  input  in_6,
  input  in_7,
  input  in_8,
  input  in_9,
  input  in_10,
  input  in_11,
  output Overflow,
  output out_13,
  output out_14,
  output out_15,
  output out_16,
  output out_17,
  output Overflow_2,
  output out_19,
  output out_20,
  output out_21,
  output out_22,
  output out_23
);

  wire and_1_out, and_2_out, and_3_out, and_4_out, and_5_out, and_6_out, and_7_out, and_8_out, and_9_out,
       and_10_out, and_11_out, and_12_out, and_13_out, and_15_out, and_16_out, and_17_out, and_18_out,
       and_19_out, and_20_out, and_21_out, and_22_out, and_23_out, and_24_out, and_25_out, and_26_out,
       and_27_out, and_28_out, and_29_out, and_30_out, and_31_out, and_32_out, and_33_out, and_34_out,
       and_35_out, and_36_out, and_37_out, not_1_out, not_2_out, not_3_out, not_4_out, not_5_out, not_6_out,
       not_7_out, not_8_out, not_9_out, not_10_out, not_11_out, not_12_out, not_13_out, not_14_out,
       not_15_out, not_16_out, not_17_out, not_18_out, not_19_out, not_20_out, not_21_out, not_22_out,
       not_23_out, not_24_out, not_25_out, not_26_out, not_27_out, not_28_out, not_29_out, not_30_out,
       not_31_out, not_32_out, not_33_out, not_34_out, not_35_out, not_36_out, not_37_out, or_1_out,
       or_2_out, or_3_out, or_4_out, or_6_out, or_7_out, or_8_out, or_9_out, or_10_out, or_11_out, or_12_out,
       or_13_out, or_14_out, xnor_1_out, xnor_2_out, xnor_3_out, xnor_4_out, xor_1_out, xor_2_out, xor_3_out,
       xor_4_out, xor_5_out, xor_6_out, xor_7_out, xor_8_out, xor_9_out, xor_10_out, xor_16_out, xor_17_out,
       xor_18_out, xor_19_out;

  xor xor_1 (xor_1_out, in_1, in_11);
  xor xor_2 (xor_2_out, in_1, in_10);
  xor xor_3 (xor_3_out, in_1, in_9);
  xor xor_4 (xor_4_out, in_1, in_8);
  xor xor_5 (xor_5_out, in_1, in_7);
  xor xor_6 (xor_6_out, in_6, xor_1_out);
  and and_1 (and_1_out, in_6, xor_1_out);
  xor xor_7 (xor_7_out, in_5, xor_2_out);
  and and_2 (and_2_out, in_5, xor_2_out);
  xor xor_8 (xor_8_out, in_4, xor_3_out);
  and and_3 (and_3_out, in_4, xor_3_out);
  xor xor_9 (xor_9_out, in_3, xor_4_out);
  and and_4 (and_4_out, in_3, xor_4_out);
  xor xor_10 (xor_10_out, in_2, xor_5_out);
  and and_5 (and_5_out, in_2, xor_5_out);
  xor xor_11 (out_17, xor_6_out, in_1);
  and and_6 (and_6_out, xor_6_out, in_1);
  xor xor_12 (out_16, xor_7_out, or_1_out);
  and and_7 (and_7_out, xor_7_out, or_1_out);
  xor xor_13 (out_15, xor_8_out, or_2_out);
  and and_8 (and_8_out, xor_8_out, or_2_out);
  xor xor_14 (out_14, xor_9_out, or_3_out);
  and and_9 (and_9_out, xor_9_out, or_3_out);
  xor xor_15 (out_13, xor_10_out, or_4_out);
  and and_10 (and_10_out, xor_10_out, or_4_out);
  or or_1 (or_1_out, and_6_out, and_1_out);
  or or_2 (or_2_out, and_7_out, and_2_out);
  or or_3 (or_3_out, and_8_out, and_3_out);
  or or_4 (or_4_out, and_9_out, and_4_out);
  or or_5 (Overflow, and_10_out, and_5_out);
  xor xor_16 (xor_16_out, out_17, out_13);
  xor xor_17 (xor_17_out, out_16, out_13);
  xor xor_18 (xor_18_out, out_15, out_13);
  xor xor_19 (xor_19_out, out_14, out_13);
  xor xor_20 (out_22, out_13, xor_16_out);
  and and_11 (and_11_out, out_13, xor_16_out);
  xor xor_21 (out_21, and_11_out, xor_17_out);
  and and_12 (and_12_out, and_11_out, xor_17_out);
  and and_13 (and_13_out, and_12_out, xor_18_out);
  xor xor_22 (out_19, and_13_out, xor_19_out);
  and and_14 (Overflow_2, and_13_out, xor_19_out);
  xor xor_23 (out_20, and_12_out, xor_18_out);
  not not_1 (not_1_out, out_19);
  not not_2 (not_2_out, out_20);
  not not_3 (not_3_out, out_21);
  not not_4 (not_4_out, out_22);
  xnor xnor_1 (xnor_1_out, 1'b1, out_19);
  and and_15 (and_15_out, 1'b1, not_1_out);
  xnor xnor_2 (xnor_2_out, 1'b0, out_20);
  and and_16 (and_16_out, 1'b0, not_2_out);
  xnor xnor_3 (xnor_3_out, 1'b1, out_21);
  and and_17 (and_17_out, 1'b1, not_3_out);
  xnor xnor_4 (xnor_4_out, 1'b0, out_22);
  and and_18 (and_18_out, 1'b0, not_4_out);
  and and_19 (and_19_out, xnor_1_out, and_16_out);
  and and_20 (and_20_out, xnor_1_out, xnor_2_out, and_17_out);
  and and_21 (and_21_out, xnor_1_out, xnor_2_out, and_18_out, xnor_3_out);
  or or_6 (or_6_out, and_15_out, and_19_out, and_20_out, and_21_out);
  not not_5 (not_5_out, out_22);
  not not_6 (not_6_out, out_19);
  not not_7 (not_7_out, out_20);
  not not_8 (not_8_out, out_21);
  not not_9 (not_9_out, out_19);
  not not_10 (not_10_out, out_20);
  not not_11 (not_11_out, out_21);
  not not_12 (not_12_out, out_19);
  not not_13 (not_13_out, out_20);
  not not_14 (not_14_out, out_22);
  not not_15 (not_15_out, out_19);
  not not_16 (not_16_out, out_20);
  not not_17 (not_17_out, out_19);
  not not_18 (not_18_out, out_21);
  not not_19 (not_19_out, out_22);
  not not_20 (not_20_out, out_19);
  not not_21 (not_21_out, out_21);
  not not_22 (not_22_out, out_19);
  not not_23 (not_23_out, out_22);
  not not_24 (not_24_out, out_19);
  not not_25 (not_25_out, out_20);
  not not_26 (not_26_out, out_21);
  not not_27 (not_27_out, out_22);
  not not_28 (not_28_out, out_20);
  not not_29 (not_29_out, out_21);
  not not_30 (not_30_out, out_20);
  not not_31 (not_31_out, out_22);
  not not_32 (not_32_out, out_20);
  not not_33 (not_33_out, out_21);
  not not_34 (not_34_out, out_22);
  not not_35 (not_35_out, out_21);
  not not_36 (not_36_out, out_22);
  and and_22 (and_22_out, not_5_out, not_6_out, not_7_out, not_8_out, not_8_out);
  and and_23 (and_23_out, not_9_out, not_10_out, not_11_out, out_22);
  and and_24 (and_24_out, not_12_out, not_13_out, out_21, not_14_out);
  and and_25 (and_25_out, not_15_out, not_16_out, out_21, out_22);
  and and_26 (and_26_out, not_17_out, out_20, not_18_out, not_19_out);
  and and_27 (and_27_out, not_20_out, out_20, not_21_out, out_22);
  and and_28 (and_28_out, not_22_out, out_20, out_21, not_23_out);
  and and_29 (and_29_out, not_24_out, out_20, out_21, out_22);
  and and_30 (and_30_out, out_19, not_25_out, not_26_out, not_27_out);
  and and_31 (and_31_out, out_19, not_28_out, not_29_out, out_22);
  and and_32 (and_32_out, out_19, not_30_out, out_21, not_31_out);
  and and_33 (and_33_out, out_19, not_32_out, out_21, out_22);
  and and_34 (and_34_out, out_19, out_20, not_33_out, not_34_out);
  and and_35 (and_35_out, out_19, out_20, not_35_out, out_22);
  and and_36 (and_36_out, out_19, out_20, out_21, not_36_out);
  and and_37 (and_37_out, out_19, out_20, out_21, out_22);
  or or_7 (or_7_out, and_29_out, and_22_out, and_24_out, and_25_out, and_27_out, and_28_out, and_30_out, and_31_out, and_32_out, and_34_out, and_35_out, and_37_out);
  or or_8 (or_8_out, and_22_out, and_24_out, and_23_out, and_25_out, and_26_out, and_35_out, and_36_out, and_34_out, and_29_out, and_30_out, and_31_out, and_32_out, and_33_out);
  or or_9 (or_9_out, and_29_out, and_22_out, and_23_out, and_25_out, and_26_out, and_27_out, and_28_out, and_30_out, and_31_out, and_32_out, and_33_out, and_35_out, and_36_out, and_37_out);
  or or_10 (or_10_out, and_22_out, and_24_out, and_25_out, and_30_out, and_27_out, and_28_out, and_31_out, and_32_out, and_34_out, and_35_out, and_37_out);
  or or_11 (or_11_out, and_22_out, and_24_out, and_28_out, and_30_out, and_32_out, and_34_out);
  or or_12 (or_12_out, and_37_out, and_22_out, and_26_out, and_27_out, and_28_out, and_30_out, and_32_out, and_31_out, and_36_out);
  or or_13 (or_13_out, and_24_out, and_25_out, and_37_out, and_26_out, and_27_out, and_28_out, and_31_out, and_30_out, and_36_out, and_34_out, and_35_out);
  _7_Segment_Display u_7_segment_display_1 (
    .f(or_6_out), .a(or_6_out), .b(or_14_out), .e(or_6_out), .d(or_6_out), .c(or_14_out));  // open: g, dp
  _7_Segment_Display u_7_segment_display_2 (.g(out_13));  // open: f, a, b, e, d, c, dp
  or or_14 (or_14_out, or_6_out, not_37_out);
  not not_37 (not_37_out, or_6_out);
  _7_Segment_Display u_7_segment_display_3 (
    .g(or_13_out), .f(or_12_out), .a(or_7_out), .b(or_8_out), .e(or_11_out), .d(or_10_out), .c(or_9_out));  // open: dp

  assign out_23 = out_13;

  // Notes on the sheet:
  //   Numero En Complemento a 2
  //   Signo(1 es Negativo)
  //   Numero en Binario
endmodule
