// Logisim project BusBidireccional.circ as structural Verilog: 1 circuit, main circuit main
module main (
  input  in_1,
  input  [1:0] in_2,
  input  in_3,
  input  in_4,
  input  in_5,
  input  in_6,
  output out_7,
  output out_8
);

  wire controlled_buffer_2_out, decoder_1_out0, decoder_1_out1, decoder_1_out2, decoder_1_out3, not_1_out,
       not_2_out;

  assign out_7 = not_1_out ? controlled_buffer_2_out : 1'bz;  // Controlled_Buffer controlled_buffer_1
  assign controlled_buffer_2_out = in_1 ? out_7 : 1'bz;  // Controlled_Buffer controlled_buffer_2
  not not_1 (not_1_out, in_1);
  assign controlled_buffer_2_out = decoder_1_out0 ? in_3 : 1'bz;  // Controlled_Buffer controlled_buffer_3
  assign controlled_buffer_2_out = decoder_1_out1 ? in_4 : 1'bz;  // Controlled_Buffer controlled_buffer_4
  assign controlled_buffer_2_out = decoder_1_out2 ? in_5 : 1'bz;  // Controlled_Buffer controlled_buffer_5
  assign controlled_buffer_2_out = decoder_1_out3 ? in_6 : 1'bz;  // Controlled_Buffer controlled_buffer_6
  Decoder #(.select(2), .enable("false")) decoder_1 (
    .out0(decoder_1_out0), .out1(decoder_1_out1), .out2(decoder_1_out2), .out3(decoder_1_out3), .sel(in_2));
  not not_2 (not_2_out, in_1);
  assign controlled_buffer_2_out = not_2_out ? out_8 : 1'bz;  // Controlled_Buffer controlled_buffer_7
  assign out_8 = in_1 ? controlled_buffer_2_out : 1'bz;  // Controlled_Buffer controlled_buffer_8
endmodule
