// Logisim project SistemaDeBusYRegistros.circ as structural Verilog: 1 circuit, main circuit main
module main (
  input  [7:0] in_1
);

  wire clock_1_out, controlled_buffer_9_out, controlled_buffer_10_out, controlled_buffer_13_out,
       controlled_buffer_14_out, controlled_buffer_17_out, controlled_buffer_18_out,
       controlled_buffer_21_out, controlled_buffer_22_out, controlled_buffer_25_out,
       controlled_buffer_26_out, controlled_buffer_29_out, controlled_buffer_30_out,
       controlled_buffer_33_out, controlled_buffer_34_out, controlled_buffer_37_out,
       controlled_buffer_38_out, d_ff_1_q, d_ff_2_q, d_ff_3_q, d_ff_4_q, d_ff_5_q, d_ff_6_q, d_ff_7_q,
       d_ff_8_q, d_ff_9_q, d_ff_10_q, d_ff_11_q, d_ff_12_q, d_ff_13_q, d_ff_14_q, d_ff_15_q, d_ff_16_q,
       decoder_1_out0, decoder_1_out1, not_1_out, not_2_out, not_3_out, not_4_out, not_5_out, undriven;
  wire [7:0] ram_1_data;

  Clock clock_1 (.out(clock_1_out));
  RAM #(.databus("bidir")) ram_1 (.clk(clock_1_out), .data(ram_1_data));  // open: addr, we, oe
  Controlled_Buffer controlled_buffer_1 (.in(in_1[7]), .out(ram_1_data[7]));  // open: en
  Controlled_Buffer controlled_buffer_2 (.in(in_1[6]), .out(ram_1_data[6]));  // open: en
  Controlled_Buffer controlled_buffer_3 (.in(in_1[5]), .out(ram_1_data[5]));  // open: en
  Controlled_Buffer controlled_buffer_4 (.in(in_1[4]), .out(ram_1_data[4]));  // open: en
  assign ram_1_data[3] = decoder_1_out0 ? in_1[7] : 1'bz;  // Controlled_Buffer controlled_buffer_5
  assign ram_1_data[2] = decoder_1_out0 ? in_1[6] : 1'bz;  // Controlled_Buffer controlled_buffer_6
  assign ram_1_data[1] = decoder_1_out0 ? in_1[5] : 1'bz;  // Controlled_Buffer controlled_buffer_7
  assign ram_1_data[0] = decoder_1_out0 ? in_1[4] : 1'bz;  // Controlled_Buffer controlled_buffer_8
  Decoder #(.select(4)) decoder_1 (
    .out0(decoder_1_out0), .out1(decoder_1_out1), .sel(in_1[3:0]), .en(clock_1_out));  // open: out2, out3, out4, out5, out6, out7, out8, out9, out10, out11, out12, out13, out14, out15
  D_Flip_Flop d_ff_1 (.D(controlled_buffer_9_out), .clk(clock_1_out), .Q(d_ff_1_q));  // open: Qn, preset, reset
  assign controlled_buffer_9_out = decoder_1_out1 ? ram_1_data[7] : 1'bz;  // Controlled_Buffer controlled_buffer_9
  Controlled_Buffer controlled_buffer_10 (.in(ram_1_data[7]), .out(controlled_buffer_10_out));  // open: en
  D_Flip_Flop d_ff_2 (.D(controlled_buffer_10_out), .clk(clock_1_out), .Q(d_ff_2_q));  // open: Qn, preset, reset
  Controlled_Buffer controlled_buffer_11 (.in(d_ff_1_q), .out(ram_1_data[7]));  // open: en
  Controlled_Buffer controlled_buffer_12 (.in(d_ff_2_q), .out(ram_1_data[7]));  // open: en
  assign controlled_buffer_13_out = decoder_1_out1 ? ram_1_data[6] : 1'bz;  // Controlled_Buffer controlled_buffer_13
  Controlled_Buffer controlled_buffer_14 (.in(ram_1_data[6]), .out(controlled_buffer_14_out));  // open: en
  D_Flip_Flop d_ff_3 (.D(controlled_buffer_13_out), .clk(clock_1_out), .Q(d_ff_3_q));  // open: Qn, preset, reset
  D_Flip_Flop d_ff_4 (.D(controlled_buffer_14_out), .clk(clock_1_out), .Q(d_ff_4_q));  // open: Qn, preset, reset
  Controlled_Buffer controlled_buffer_15 (.in(d_ff_3_q), .out(ram_1_data[6]));  // open: en
  Controlled_Buffer controlled_buffer_16 (.in(d_ff_4_q), .out(ram_1_data[6]));  // open: en
  D_Flip_Flop d_ff_5 (.D(controlled_buffer_17_out), .clk(clock_1_out), .Q(d_ff_5_q));  // open: Qn, preset, reset
  assign controlled_buffer_17_out = decoder_1_out1 ? ram_1_data[5] : 1'bz;  // Controlled_Buffer controlled_buffer_17
  Controlled_Buffer controlled_buffer_18 (.in(ram_1_data[5]), .out(controlled_buffer_18_out));  // open: en
  D_Flip_Flop d_ff_6 (.D(controlled_buffer_18_out), .clk(clock_1_out), .Q(d_ff_6_q));  // open: Qn, preset, reset
  Controlled_Buffer controlled_buffer_19 (.in(d_ff_5_q), .out(ram_1_data[5]));  // open: en
  Controlled_Buffer controlled_buffer_20 (.in(d_ff_6_q), .out(ram_1_data[5]));  // open: en
  D_Flip_Flop d_ff_7 (
    .D(controlled_buffer_21_out), .clk(clock_1_out), .Q(d_ff_7_q), .reset(not_1_out));  // open: Qn, preset
  assign controlled_buffer_21_out = decoder_1_out1 ? ram_1_data[4] : 1'bz;  // Controlled_Buffer controlled_buffer_21
  Controlled_Buffer controlled_buffer_22 (.in(ram_1_data[4]), .out(controlled_buffer_22_out));  // open: en
  D_Flip_Flop d_ff_8 (.D(controlled_buffer_22_out), .clk(clock_1_out), .Q(d_ff_8_q));  // open: Qn, preset, reset
  not not_1 (not_1_out, controlled_buffer_21_out);
  Controlled_Buffer controlled_buffer_23 (.in(d_ff_7_q), .out(ram_1_data[4]));  // open: en
  Controlled_Buffer controlled_buffer_24 (.in(d_ff_8_q), .out(ram_1_data[4]));  // open: en
  assign controlled_buffer_25_out = decoder_1_out0 ? ram_1_data[3] : 1'bz;  // Controlled_Buffer controlled_buffer_25
  Controlled_Buffer controlled_buffer_26 (.in(ram_1_data[3]), .out(controlled_buffer_26_out));  // open: en
  D_Flip_Flop d_ff_9 (
    .clk(clock_1_out), .Q(d_ff_9_q), .preset(controlled_buffer_25_out), .reset(not_2_out));  // open: D, Qn
  not not_2 (not_2_out, controlled_buffer_25_out);
  D_Flip_Flop d_ff_10 (.D(controlled_buffer_26_out), .clk(clock_1_out), .Q(d_ff_10_q));  // open: Qn, preset, reset
  Controlled_Buffer controlled_buffer_27 (.in(d_ff_9_q), .out(ram_1_data[3]));  // open: en
  Controlled_Buffer controlled_buffer_28 (.in(d_ff_10_q), .out(ram_1_data[3]));  // open: en
  D_Flip_Flop d_ff_11 (
    .clk(clock_1_out), .Q(d_ff_11_q), .preset(controlled_buffer_29_out), .reset(not_3_out));  // open: D, Qn
  assign controlled_buffer_29_out = decoder_1_out0 ? ram_1_data[2] : 1'bz;  // Controlled_Buffer controlled_buffer_29
  Controlled_Buffer controlled_buffer_30 (.in(ram_1_data[2]), .out(controlled_buffer_30_out));  // open: en
  D_Flip_Flop d_ff_12 (.D(controlled_buffer_30_out), .clk(clock_1_out), .Q(d_ff_12_q));  // open: Qn, preset, reset
  not not_3 (not_3_out, controlled_buffer_29_out);
  Controlled_Buffer controlled_buffer_31 (.in(d_ff_11_q), .out(ram_1_data[2]));  // open: en
  Controlled_Buffer controlled_buffer_32 (.in(d_ff_12_q), .out(ram_1_data[2]));  // open: en
  D_Flip_Flop d_ff_13 (
    .clk(clock_1_out), .Q(d_ff_13_q), .preset(controlled_buffer_33_out), .reset(not_4_out));  // open: D, Qn
  not not_4 (not_4_out, controlled_buffer_33_out);
  assign controlled_buffer_33_out = decoder_1_out0 ? ram_1_data[1] : 1'bz;  // Controlled_Buffer controlled_buffer_33
  Controlled_Buffer controlled_buffer_34 (.in(ram_1_data[1]), .out(controlled_buffer_34_out));  // open: en
  D_Flip_Flop d_ff_14 (.D(controlled_buffer_34_out), .clk(clock_1_out), .Q(d_ff_14_q));  // open: Qn, preset, reset
  Controlled_Buffer controlled_buffer_35 (.in(d_ff_13_q), .out(ram_1_data[1]));  // open: en
  Controlled_Buffer controlled_buffer_36 (.in(d_ff_14_q), .out(ram_1_data[1]));  // open: en
  assign controlled_buffer_37_out = decoder_1_out0 ? ram_1_data[0] : 1'bz;  // Controlled_Buffer controlled_buffer_37
  Controlled_Buffer controlled_buffer_38 (.in(ram_1_data[0]), .out(controlled_buffer_38_out));  // open: en
  D_Flip_Flop d_ff_15 (
    .D(undriven), .clk(clock_1_out), .Q(d_ff_15_q), .preset(controlled_buffer_37_out), .reset(not_5_out));  // open: Qn
  not not_5 (not_5_out, controlled_buffer_37_out);
  Controlled_Buffer controlled_buffer_39 (.in(d_ff_15_q), .out(ram_1_data[0]));  // open: en
  Controlled_Buffer controlled_buffer_40 (.in(d_ff_16_q), .out(ram_1_data[0]));  // open: en
  D_Flip_Flop d_ff_16 (.D(controlled_buffer_38_out), .clk(clock_1_out), .Q(d_ff_16_q));  // open: Qn, preset, reset
endmodule
