// Logisim project SistemaDeRegistrosV2.circ as structural Verilog: 1 circuit, main circuit main
module main (
  input  [7:0] in_1
);

  wire clock_1_out, controlled_buffer_9_out, controlled_buffer_10_out, controlled_buffer_11_out,
       controlled_buffer_13_out, controlled_buffer_15_out, controlled_buffer_17_out,
       controlled_buffer_19_out, controlled_buffer_21_out, controlled_buffer_25_out,
       controlled_buffer_26_out, controlled_buffer_29_out, controlled_buffer_30_out,
       controlled_buffer_33_out, controlled_buffer_34_out, controlled_buffer_35_out,
       controlled_buffer_37_out, d_ff_1_q, d_ff_2_q, d_ff_3_q, d_ff_4_q, d_ff_5_q, d_ff_6_q, d_ff_7_q,
       d_ff_8_q, d_ff_9_q, d_ff_10_q, d_ff_11_q, d_ff_12_q, d_ff_13_q, d_ff_14_q, d_ff_15_q, d_ff_16_q,
       decoder_1_out0, decoder_1_out1, decoder_1_out2, decoder_1_out3, decoder_1_out4, decoder_1_out5,
       decoder_1_out6, decoder_1_out7, not_1_out, not_2_out, not_3_out, not_4_out, not_5_out, not_6_out,
       not_7_out, not_8_out, not_9_out, not_10_out, not_11_out, not_12_out, not_13_out, not_14_out,
       not_15_out, not_16_out, or_1_out, or_2_out, or_3_out, or_4_out, or_5_out, or_6_out, or_7_out,
       or_8_out, or_9_out, or_10_out;
  wire [7:0] controlled_buffer_8_out, controlled_buffer_41_out;

  Clock clock_1 (.out(clock_1_out));
  assign controlled_buffer_8_out[7] = or_2_out ? in_1[7] : 1'bz;  // Controlled_Buffer controlled_buffer_1
  assign controlled_buffer_8_out[6] = or_2_out ? in_1[6] : 1'bz;  // Controlled_Buffer controlled_buffer_2
  assign controlled_buffer_8_out[5] = or_2_out ? in_1[5] : 1'bz;  // Controlled_Buffer controlled_buffer_3
  assign controlled_buffer_8_out[4] = or_2_out ? in_1[4] : 1'bz;  // Controlled_Buffer controlled_buffer_4
  assign controlled_buffer_8_out[3] = or_1_out ? in_1[7] : 1'bz;  // Controlled_Buffer controlled_buffer_5
  assign controlled_buffer_8_out[2] = or_1_out ? in_1[6] : 1'bz;  // Controlled_Buffer controlled_buffer_6
  assign controlled_buffer_8_out[1] = or_1_out ? in_1[5] : 1'bz;  // Controlled_Buffer controlled_buffer_7
  assign controlled_buffer_8_out[0] = or_1_out ? in_1[4] : 1'bz;  // Controlled_Buffer controlled_buffer_8
  or or_1 (or_1_out, decoder_1_out0, decoder_1_out2);
  or or_2 (or_2_out, decoder_1_out1, decoder_1_out3);
  assign controlled_buffer_9_out = or_4_out ? controlled_buffer_8_out[7] : 1'bz;  // Controlled_Buffer controlled_buffer_9
  assign controlled_buffer_10_out = or_3_out ? controlled_buffer_8_out[7] : 1'bz;  // Controlled_Buffer controlled_buffer_10
  D_Flip_Flop d_ff_1 (
    .clk(clock_1_out), .Q(d_ff_1_q), .preset(controlled_buffer_9_out), .reset(not_1_out));  // open: D, Qn
  not not_1 (not_1_out, controlled_buffer_9_out);
  D_Flip_Flop d_ff_2 (
    .clk(clock_1_out), .Q(d_ff_2_q), .preset(controlled_buffer_10_out), .reset(not_2_out));  // open: D, Qn
  not not_2 (not_2_out, controlled_buffer_10_out);
  Decoder #(.select(4)) decoder_1 (
    .out0(decoder_1_out0), .out1(decoder_1_out1), .out2(decoder_1_out2), .out3(decoder_1_out3),
    .out4(decoder_1_out4), .out5(decoder_1_out5), .out6(decoder_1_out6), .out7(decoder_1_out7),
    .sel(in_1[3:0]), .en(clock_1_out));  // open: out8, out9, out10, out11, out12, out13, out14, out15
  assign controlled_buffer_11_out = or_4_out ? controlled_buffer_8_out[6] : 1'bz;  // Controlled_Buffer controlled_buffer_11
  assign controlled_buffer_8_out[7] = decoder_1_out4 ? d_ff_1_q : 1'bz;  // Controlled_Buffer controlled_buffer_12
  assign controlled_buffer_13_out = or_3_out ? controlled_buffer_8_out[6] : 1'bz;  // Controlled_Buffer controlled_buffer_13
  assign controlled_buffer_8_out[7] = decoder_1_out5 ? d_ff_2_q : 1'bz;  // Controlled_Buffer controlled_buffer_14
  D_Flip_Flop d_ff_3 (
    .clk(clock_1_out), .Q(d_ff_3_q), .preset(controlled_buffer_11_out), .reset(not_3_out));  // open: D, Qn
  not not_3 (not_3_out, controlled_buffer_11_out);
  D_Flip_Flop d_ff_4 (
    .clk(clock_1_out), .Q(d_ff_4_q), .preset(controlled_buffer_13_out), .reset(not_4_out));  // open: D, Qn
  not not_4 (not_4_out, controlled_buffer_13_out);
  or or_3 (or_3_out, decoder_1_out7, decoder_1_out3);
  assign controlled_buffer_15_out = or_4_out ? controlled_buffer_8_out[5] : 1'bz;  // Controlled_Buffer controlled_buffer_15
  assign controlled_buffer_8_out[6] = decoder_1_out4 ? d_ff_3_q : 1'bz;  // Controlled_Buffer controlled_buffer_16
  assign controlled_buffer_17_out = or_3_out ? controlled_buffer_8_out[5] : 1'bz;  // Controlled_Buffer controlled_buffer_17
  assign controlled_buffer_8_out[6] = decoder_1_out5 ? d_ff_4_q : 1'bz;  // Controlled_Buffer controlled_buffer_18
  D_Flip_Flop d_ff_5 (
    .clk(clock_1_out), .Q(d_ff_5_q), .preset(controlled_buffer_15_out), .reset(not_5_out));  // open: D, Qn
  not not_5 (not_5_out, controlled_buffer_15_out);
  D_Flip_Flop d_ff_6 (
    .clk(clock_1_out), .Q(d_ff_6_q), .preset(controlled_buffer_17_out), .reset(not_6_out));  // open: D, Qn
  not not_6 (not_6_out, controlled_buffer_17_out);
  D_Flip_Flop d_ff_7 (
    .clk(clock_1_out), .Q(d_ff_7_q), .preset(controlled_buffer_19_out), .reset(not_7_out));  // open: D, Qn
  assign controlled_buffer_19_out = or_4_out ? controlled_buffer_8_out[4] : 1'bz;  // Controlled_Buffer controlled_buffer_19
  assign controlled_buffer_8_out[5] = decoder_1_out4 ? d_ff_5_q : 1'bz;  // Controlled_Buffer controlled_buffer_20
  D_Flip_Flop d_ff_8 (
    .clk(clock_1_out), .Q(d_ff_8_q), .preset(controlled_buffer_21_out), .reset(not_8_out));  // open: D, Qn
  assign controlled_buffer_21_out = or_3_out ? controlled_buffer_8_out[4] : 1'bz;  // Controlled_Buffer controlled_buffer_21
  assign controlled_buffer_8_out[5] = decoder_1_out5 ? d_ff_6_q : 1'bz;  // Controlled_Buffer controlled_buffer_22
  not not_7 (not_7_out, controlled_buffer_19_out);
  assign controlled_buffer_8_out[4] = decoder_1_out4 ? d_ff_7_q : 1'bz;  // Controlled_Buffer controlled_buffer_23
  not not_8 (not_8_out, controlled_buffer_21_out);
  assign controlled_buffer_8_out[4] = decoder_1_out5 ? d_ff_8_q : 1'bz;  // Controlled_Buffer controlled_buffer_24
  or or_4 (or_4_out, decoder_1_out6, decoder_1_out1);
  D_Flip_Flop d_ff_9 (
    .clk(clock_1_out), .Q(d_ff_9_q), .preset(controlled_buffer_25_out), .reset(not_9_out));  // open: D, Qn
  assign controlled_buffer_25_out = or_5_out ? controlled_buffer_8_out[3] : 1'bz;  // Controlled_Buffer controlled_buffer_25
  D_Flip_Flop d_ff_10 (
    .clk(clock_1_out), .Q(d_ff_10_q), .preset(controlled_buffer_26_out), .reset(not_10_out));  // open: D, Qn
  assign controlled_buffer_26_out = or_7_out ? controlled_buffer_8_out[3] : 1'bz;  // Controlled_Buffer controlled_buffer_26
  not not_9 (not_9_out, controlled_buffer_25_out);
  assign controlled_buffer_8_out[3] = decoder_1_out4 ? d_ff_9_q : 1'bz;  // Controlled_Buffer controlled_buffer_27
  not not_10 (not_10_out, controlled_buffer_26_out);
  assign controlled_buffer_8_out[3] = decoder_1_out5 ? d_ff_10_q : 1'bz;  // Controlled_Buffer controlled_buffer_28
  D_Flip_Flop d_ff_11 (
    .clk(clock_1_out), .Q(d_ff_11_q), .preset(controlled_buffer_29_out), .reset(not_11_out));  // open: D, Qn
  not not_11 (not_11_out, controlled_buffer_29_out);
  assign controlled_buffer_29_out = or_5_out ? controlled_buffer_8_out[2] : 1'bz;  // Controlled_Buffer controlled_buffer_29
  D_Flip_Flop d_ff_12 (
    .clk(clock_1_out), .Q(d_ff_12_q), .preset(controlled_buffer_30_out), .reset(not_12_out));  // open: D, Qn
  not not_12 (not_12_out, controlled_buffer_30_out);
  assign controlled_buffer_30_out = or_7_out ? controlled_buffer_8_out[2] : 1'bz;  // Controlled_Buffer controlled_buffer_30
  assign controlled_buffer_8_out[2] = decoder_1_out4 ? d_ff_11_q : 1'bz;  // Controlled_Buffer controlled_buffer_31
  assign controlled_buffer_8_out[2] = decoder_1_out5 ? d_ff_12_q : 1'bz;  // Controlled_Buffer controlled_buffer_32
  D_Flip_Flop d_ff_13 (
    .clk(clock_1_out), .Q(d_ff_13_q), .preset(controlled_buffer_33_out), .reset(not_13_out));  // open: D, Qn
  not not_13 (not_13_out, controlled_buffer_33_out);
  assign controlled_buffer_33_out = or_5_out ? controlled_buffer_8_out[1] : 1'bz;  // Controlled_Buffer controlled_buffer_33
  D_Flip_Flop d_ff_14 (
    .clk(clock_1_out), .Q(d_ff_14_q), .preset(controlled_buffer_34_out), .reset(not_14_out));  // open: D, Qn
  not not_14 (not_14_out, controlled_buffer_34_out);
  assign controlled_buffer_34_out = or_7_out ? controlled_buffer_8_out[1] : 1'bz;  // Controlled_Buffer controlled_buffer_34
  assign controlled_buffer_35_out = or_5_out ? controlled_buffer_8_out[0] : 1'bz;  // Controlled_Buffer controlled_buffer_35
  assign controlled_buffer_8_out[1] = decoder_1_out4 ? d_ff_13_q : 1'bz;  // Controlled_Buffer controlled_buffer_36
  assign controlled_buffer_37_out = or_7_out ? controlled_buffer_8_out[0] : 1'bz;  // Controlled_Buffer controlled_buffer_37
  assign controlled_buffer_8_out[1] = decoder_1_out5 ? d_ff_14_q : 1'bz;  // Controlled_Buffer controlled_buffer_38
  D_Flip_Flop d_ff_15 (
    .clk(clock_1_out), .Q(d_ff_15_q), .preset(controlled_buffer_35_out), .reset(not_15_out));  // open: D, Qn
  not not_15 (not_15_out, controlled_buffer_35_out);
  D_Flip_Flop d_ff_16 (
    .clk(clock_1_out), .Q(d_ff_16_q), .preset(controlled_buffer_37_out), .reset(not_16_out));  // open: D, Qn
  not not_16 (not_16_out, controlled_buffer_37_out);
  or or_5 (or_5_out, decoder_1_out6, decoder_1_out0);
  assign controlled_buffer_8_out[0] = decoder_1_out4 ? d_ff_15_q : 1'bz;  // Controlled_Buffer controlled_buffer_39
  assign controlled_buffer_8_out[0] = decoder_1_out5 ? d_ff_16_q : 1'bz;  // Controlled_Buffer controlled_buffer_40
  or or_6 (or_6_out, decoder_1_out4, decoder_1_out5);
  or or_7 (or_7_out, decoder_1_out7, decoder_1_out2);
  assign controlled_buffer_41_out[0] = or_8_out ? in_1[4] : 1'bz;  // Controlled_Buffer controlled_buffer_41
  assign controlled_buffer_41_out[1] = or_8_out ? in_1[5] : 1'bz;  // Controlled_Buffer controlled_buffer_42
  assign controlled_buffer_41_out[2] = or_8_out ? in_1[6] : 1'bz;  // Controlled_Buffer controlled_buffer_43
  assign controlled_buffer_41_out[3] = or_8_out ? in_1[7] : 1'bz;  // Controlled_Buffer controlled_buffer_44
  or or_8 (or_8_out, decoder_1_out6, decoder_1_out4, decoder_1_out5, decoder_1_out7);
  or or_9 (or_9_out, decoder_1_out6, decoder_1_out7);
  assign controlled_buffer_41_out[7] = or_8_out ? 1'b0 : 1'bz;  // Controlled_Buffer controlled_buffer_45
  assign controlled_buffer_41_out[6] = or_8_out ? 1'b0 : 1'bz;  // Controlled_Buffer controlled_buffer_46
  assign controlled_buffer_41_out[5] = or_8_out ? 1'b0 : 1'bz;  // Controlled_Buffer controlled_buffer_47
  assign controlled_buffer_41_out[4] = or_8_out ? 1'b0 : 1'bz;  // Controlled_Buffer controlled_buffer_48
  or or_10 (or_10_out, or_6_out, or_9_out);
  RAM #(.asyncread("true"), .clearpin("true"), .databus("bidir")) ram_1 (
    .addr(controlled_buffer_41_out), .we(or_6_out), .oe(or_9_out), .clk(or_10_out),
    .data(controlled_buffer_8_out));  // open: clr
endmodule
